# Fritzing sketch Tipsy_Schematic (saved by Fritzing 0.9.2b)
stripboards: 4

parts:
  Part1 = Motor Driver 1A Dual TB6612FNG  # not connected
  VCC1 = Battery  # not connected
  VCC2 = Battery
  IC1 = Voltage Regulator [package=to-220-alt]
  J8 = female pin header, 2 pins [form="♀ (female)"]  # not connected
  J9 = female pin header, 2 pins [form="♀ (female)"]
  J10 = female pin header, 2 pins [form="♀ (female)"]  # not connected
  M1 = DC Motor  # not connected
  M2 = DC Motor  # not connected
  Part2 = Logic Level Converter
  U1 = Voltage Regulator [package=to220-adj]

nets:
  N1: VCC2.-, IC1.IN, IC1.OUT, J9.pin1, Part2.GND, U1.OUT
  N2: VCC2.+, U1.ADJ
  N3: Part2.TX2_LV, Part2.TX2_HV
  N4: Part2.RX2_LV, Part2.RX2_HV
  N5: Part2.LV, Part2.HV
  N6: Part2.RX_LV, Part2.RX_HV
  N7: Part2.TX_LV, Part2.TX_HV

notes:
  1
  5
  10
  15
  20
  30
  25
  50
  40
  35
  44
  55
  67
  65
  60
  45
  a     b     c     d     e
  f     g     h     i     j
  + -
  >5v RAIL
  5v RAIL
  4
  6
  2
  3
  0
  7
  VPP
  GND
  VCC
  RX
  TX
  PIN1: VPP
  PIN2: VCC
  PIN3: GND
  PIN4: RB7
  PIN6: NOT USED
  PIN5: RB6
  A01
  VM
  A02
  B01
  B02
  AI1
  AI2
  STBY
  PWMA
  BI1
  PWMB
  BI2
  MOTOR B
  MOTOR A
  Note for motors:
  Schematic Color Yellow = Red Lead
  Schematic Color Green = Black Lead
  IMU to PIC Cheatsheet
  IMU PIC
  MOSI (DA) Rx
  SCLK (CL) RB1
  MISO (AD0) RB0
  CS (NC) RB2
  VDD
  SDA
  SCL
  CS_M
  CS_AG
  SDO_AG
  NOTE: I cut the breadboard along H between 25 and 30. Otherwise the logic stepper will short
  <------------------------------
